// Logisim project 1 bit register.circ as structural Verilog: 1 circuit, main circuit main
module main (
  input  Enable,
  input  Cin,
  input  Input,
  input  Select1,
  input  Select2,
  output Cout,
  output Output
);

  wire adder_1_out, clock_1_out, multiplexer_1_out;

  Clock clock_1 (.out(clock_1_out));
  Multiplexer #(.select(2), .disabled(0), .enable("false")) multiplexer_1 (
    .in0(1'b0), .in1(adder_1_out), .in2(adder_1_out), .in3(Input), .out(multiplexer_1_out),
    .sel({Select1, Select2}));
  D_Flip_Flop d_ff_1 (.clk(clock_1_out), .D(multiplexer_1_out), .Q(Output), .en(Enable));  // open: Qn, preset, reset
  Adder #(.width(1)) adder_1 (.a(Output), .b(Select1), .out(adder_1_out), .cin(Cin), .cout(Cout));
endmodule
