// Logisim project 16-bit IR register.circ as structural Verilog: 1 circuit, main circuit main
module main (
  input  Enable,
  input  [1:0] Funcel,
  input  L1_H0,
  input  [7:0] in_4,
  output [15:0] out_5
);

  wire _1bit_Register_cout, main_1_cout, main_2_cout, main_3_cout, main_4_cout, main_5_cout, main_6_cout,
       main_7_cout, main_8_cout, main_9_cout, main_10_cout, main_11_cout, main_12_cout, main_13_cout,
       main_14_cout, not_1_out;
  wire [7:0] multiplexer_1_out, multiplexer_2_out;

  Hex_Digit_Display hex_digit_display_1 (.value(out_5[15:12]));  // open: dp
  Hex_Digit_Display hex_digit_display_2 (.value(out_5[11:8]));  // open: dp
  Hex_Digit_Display hex_digit_display_3 (.value(out_5[3:0]));  // open: dp
  Hex_Digit_Display hex_digit_display_4 (.value(out_5[7:4]));  // open: dp
  not not_1 (not_1_out, Funcel[1]);
  _1_bit_register_main _1bit_Register (
    .Cin(not_1_out), .Input(multiplexer_1_out[0]), .Enable(Enable), .Select1(Funcel[1]), .Select2(Funcel[0]),
    .Cout(_1bit_Register_cout), .Output(out_5[0]));
  Multiplexer #(.width(8), .enable("false")) multiplexer_1 (
    .in0(out_5[7:0]), .in1(in_4), .out(multiplexer_1_out), .sel(L1_H0));
  Hex_Digit_Display hex_digit_display_5 (.value(in_4[7:4]));  // open: dp
  _1_bit_register_main main_1 (
    .Cin(_1bit_Register_cout), .Input(multiplexer_1_out[1]), .Enable(Enable), .Select1(Funcel[1]),
    .Select2(Funcel[0]), .Cout(main_1_cout), .Output(out_5[1]));
  Hex_Digit_Display hex_digit_display_6 (.value(in_4[3:0]));  // open: dp
  _1_bit_register_main main_2 (
    .Cin(main_1_cout), .Input(multiplexer_1_out[2]), .Enable(Enable), .Select1(Funcel[1]),
    .Select2(Funcel[0]), .Cout(main_2_cout), .Output(out_5[2]));
  Multiplexer #(.width(8), .enable("false")) multiplexer_2 (
    .in0(in_4), .in1(out_5[15:8]), .out(multiplexer_2_out), .sel(L1_H0));
  _1_bit_register_main main_3 (
    .Cin(main_2_cout), .Input(multiplexer_1_out[3]), .Enable(Enable), .Select1(Funcel[1]),
    .Select2(Funcel[0]), .Cout(main_3_cout), .Output(out_5[3]));
  _1_bit_register_main main_4 (
    .Cin(main_3_cout), .Input(multiplexer_1_out[4]), .Enable(Enable), .Select1(Funcel[1]),
    .Select2(Funcel[0]), .Cout(main_4_cout), .Output(out_5[4]));
  _1_bit_register_main main_5 (
    .Cin(main_4_cout), .Input(multiplexer_1_out[5]), .Enable(Enable), .Select1(Funcel[1]),
    .Select2(Funcel[0]), .Cout(main_5_cout), .Output(out_5[5]));
  _1_bit_register_main main_6 (
    .Cin(main_5_cout), .Input(multiplexer_1_out[6]), .Enable(Enable), .Select1(Funcel[1]),
    .Select2(Funcel[0]), .Cout(main_6_cout), .Output(out_5[6]));
  _1_bit_register_main main_7 (
    .Cin(main_6_cout), .Input(multiplexer_1_out[7]), .Enable(Enable), .Select1(Funcel[1]),
    .Select2(Funcel[0]), .Cout(main_7_cout), .Output(out_5[7]));
  _1_bit_register_main main_8 (
    .Cin(main_7_cout), .Input(multiplexer_2_out[0]), .Enable(Enable), .Select1(Funcel[1]),
    .Select2(Funcel[0]), .Cout(main_8_cout), .Output(out_5[8]));
  _1_bit_register_main main_9 (
    .Cin(main_8_cout), .Input(multiplexer_2_out[1]), .Enable(Enable), .Select1(Funcel[1]),
    .Select2(Funcel[0]), .Cout(main_9_cout), .Output(out_5[9]));
  _1_bit_register_main main_10 (
    .Cin(main_9_cout), .Input(multiplexer_2_out[2]), .Enable(Enable), .Select1(Funcel[1]),
    .Select2(Funcel[0]), .Cout(main_10_cout), .Output(out_5[10]));
  _1_bit_register_main main_11 (
    .Cin(main_10_cout), .Input(multiplexer_2_out[3]), .Enable(Enable), .Select1(Funcel[1]),
    .Select2(Funcel[0]), .Cout(main_11_cout), .Output(out_5[11]));
  _1_bit_register_main main_12 (
    .Cin(main_11_cout), .Input(multiplexer_2_out[4]), .Enable(Enable), .Select1(Funcel[1]),
    .Select2(Funcel[0]), .Cout(main_12_cout), .Output(out_5[12]));
  _1_bit_register_main main_13 (
    .Cin(main_12_cout), .Input(multiplexer_2_out[5]), .Enable(Enable), .Select1(Funcel[1]),
    .Select2(Funcel[0]), .Cout(main_13_cout), .Output(out_5[13]));
  _1_bit_register_main main_14 (
    .Cin(main_13_cout), .Input(multiplexer_2_out[6]), .Enable(Enable), .Select1(Funcel[1]),
    .Select2(Funcel[0]), .Cout(main_14_cout), .Output(out_5[14]));
  _1_bit_register_main main_15 (
    .Cin(main_14_cout), .Input(multiplexer_2_out[7]), .Enable(Enable), .Select1(Funcel[1]),
    .Select2(Funcel[0]), .Output(out_5[15]));  // open: Cout
endmodule
