// Logisim project 16-bit register.circ as structural Verilog: 1 circuit, main circuit main
module main (
  input  Enable,
  input  [1:0] FunSel,
  input  [15:0] in_3,
  output [15:0] out_4,
  output out_5,
  output out_6,
  output out_7
);

  wire _1bit_Register_cout, main_1_cout, main_2_cout, main_3_cout, main_4_cout, main_5_cout, main_6_cout,
       main_7_cout, main_8_cout, main_9_cout, main_10_cout, main_11_cout, main_12_cout, main_13_cout,
       main_14_cout, not_1_out;

  Hex_Digit_Display hex_digit_display_1 (.value(out_4[11:8]));  // open: dp
  Hex_Digit_Display hex_digit_display_2 (.value(out_4[15:12]));  // open: dp
  Hex_Digit_Display hex_digit_display_3 (.value(out_4[7:4]));  // open: dp
  Hex_Digit_Display hex_digit_display_4 (.value(out_4[3:0]));  // open: dp
  Hex_Digit_Display hex_digit_display_5 (.value(in_3[11:8]));  // open: dp
  Hex_Digit_Display hex_digit_display_6 (.value(in_3[15:12]));  // open: dp
  not not_1 (not_1_out, FunSel[1]);
  _1_bit_register_main _1bit_Register (
    .Cin(not_1_out), .Input(in_3[0]), .Enable(Enable), .Select1(FunSel[1]), .Select2(FunSel[0]),
    .Cout(_1bit_Register_cout), .Output(out_4[0]));
  Hex_Digit_Display hex_digit_display_7 (.value(in_3[7:4]));  // open: dp
  Hex_Digit_Display hex_digit_display_8 (.value(in_3[3:0]));  // open: dp
  _1_bit_register_main main_1 (
    .Cin(_1bit_Register_cout), .Input(in_3[1]), .Enable(Enable), .Select1(FunSel[1]), .Select2(FunSel[0]),
    .Cout(main_1_cout), .Output(out_4[1]));
  _1_bit_register_main main_2 (
    .Cin(main_1_cout), .Input(in_3[2]), .Enable(Enable), .Select1(FunSel[1]), .Select2(FunSel[0]),
    .Cout(main_2_cout), .Output(out_4[2]));
  _1_bit_register_main main_3 (
    .Cin(main_2_cout), .Input(in_3[3]), .Enable(Enable), .Select1(FunSel[1]), .Select2(FunSel[0]),
    .Cout(main_3_cout), .Output(out_4[3]));
  _1_bit_register_main main_4 (
    .Cin(main_3_cout), .Input(in_3[4]), .Enable(Enable), .Select1(FunSel[1]), .Select2(FunSel[0]),
    .Cout(main_4_cout), .Output(out_4[4]));
  _1_bit_register_main main_5 (
    .Cin(main_4_cout), .Input(in_3[5]), .Enable(Enable), .Select1(FunSel[1]), .Select2(FunSel[0]),
    .Cout(main_5_cout), .Output(out_4[5]));
  _1_bit_register_main main_6 (
    .Cin(main_5_cout), .Input(in_3[6]), .Enable(Enable), .Select1(FunSel[1]), .Select2(FunSel[0]),
    .Cout(main_6_cout), .Output(out_4[6]));
  _1_bit_register_main main_7 (
    .Cin(main_6_cout), .Input(in_3[7]), .Enable(Enable), .Select1(FunSel[1]), .Select2(FunSel[0]),
    .Cout(main_7_cout), .Output(out_4[7]));
  _1_bit_register_main main_8 (
    .Cin(main_7_cout), .Input(in_3[8]), .Enable(Enable), .Select1(FunSel[1]), .Select2(FunSel[0]),
    .Cout(main_8_cout), .Output(out_4[8]));
  _1_bit_register_main main_9 (
    .Cin(main_8_cout), .Input(in_3[9]), .Enable(Enable), .Select1(FunSel[1]), .Select2(FunSel[0]),
    .Cout(main_9_cout), .Output(out_4[9]));
  _1_bit_register_main main_10 (
    .Cin(main_9_cout), .Input(in_3[10]), .Enable(Enable), .Select1(FunSel[1]), .Select2(FunSel[0]),
    .Cout(main_10_cout), .Output(out_4[10]));
  _1_bit_register_main main_11 (
    .Cin(main_10_cout), .Input(in_3[11]), .Enable(Enable), .Select1(FunSel[1]), .Select2(FunSel[0]),
    .Cout(main_11_cout), .Output(out_4[11]));
  _1_bit_register_main main_12 (
    .Cin(main_11_cout), .Input(in_3[12]), .Enable(Enable), .Select1(FunSel[1]), .Select2(FunSel[0]),
    .Cout(main_12_cout), .Output(out_4[12]));
  _1_bit_register_main main_13 (
    .Cin(main_12_cout), .Input(in_3[13]), .Enable(Enable), .Select1(FunSel[1]), .Select2(FunSel[0]),
    .Cout(main_13_cout), .Output(out_4[13]));
  _1_bit_register_main main_14 (
    .Cin(main_13_cout), .Input(in_3[14]), .Enable(Enable), .Select1(FunSel[1]), .Select2(FunSel[0]),
    .Cout(main_14_cout), .Output(out_4[14]));
  _1_bit_register_main main_15 (
    .Cin(main_14_cout), .Input(in_3[15]), .Enable(Enable), .Select1(FunSel[1]), .Select2(FunSel[0]),
    .Output(out_4[15]));  // open: Cout

  assign out_5 = Enable;
  assign out_6 = FunSel[1];
  assign out_7 = FunSel[0];
endmodule
