// Logisim project 4.circ as structural Verilog: 1 circuit, main circuit main
module main (
  input  in_1,
  input  in_2,
  input  in_3,
  input  in_4,
  input  in_5,
  input  in_6,
  output out_7,
  output out_8,
  output out_9
);

  wire multiplexer_1_out, multiplexer_2_out;

  Multiplexer #(.enable("false")) multiplexer_1 (.in0(in_1), .in1(in_3), .out(multiplexer_1_out), .sel(in_5));
  Multiplexer #(.enable("false")) multiplexer_2 (.in0(in_2), .in1(in_4), .out(multiplexer_2_out), .sel(in_5));
  Multiplexer #(.enable("false")) multiplexer_3 (
    .in0(multiplexer_1_out), .in1(multiplexer_2_out), .out(out_9), .sel(in_6));

  assign out_7 = in_5;
  assign out_8 = in_6;
endmodule
