// Logisim project 8-bit register hex---.circ as structural Verilog: 1 circuit, main circuit main
module main (
  input  [1:0] FunSel,
  input  Enable,
  input  [7:0] outA,
  output [7:0] outA_2
);

  wire _1bit_Register_cout, main_1_cout, main_2_cout, main_3_cout, main_4_cout, main_5_cout, main_6_cout,
       not_1_out;

  not not_1 (not_1_out, FunSel[1]);
  _1_bit_register_main _1bit_Register (
    .Cin(not_1_out), .Input(outA[0]), .Enable(Enable), .Select1(FunSel[1]), .Select2(FunSel[0]),
    .Cout(_1bit_Register_cout), .Output(outA_2[0]));
  _1_bit_register_main main_1 (
    .Cin(_1bit_Register_cout), .Input(outA[1]), .Enable(Enable), .Select1(FunSel[1]), .Select2(FunSel[0]),
    .Cout(main_1_cout), .Output(outA_2[1]));
  Hex_Digit_Display hex_digit_display_1 (.value(outA_2[3:0]));  // open: dp
  Hex_Digit_Display hex_digit_display_2 (.value(outA_2[7:4]));  // open: dp
  _1_bit_register_main main_2 (
    .Cin(main_1_cout), .Input(outA[2]), .Enable(Enable), .Select1(FunSel[1]), .Select2(FunSel[0]),
    .Cout(main_2_cout), .Output(outA_2[2]));
  _1_bit_register_main main_3 (
    .Cin(main_2_cout), .Input(outA[3]), .Enable(Enable), .Select1(FunSel[1]), .Select2(FunSel[0]),
    .Cout(main_3_cout), .Output(outA_2[3]));
  Hex_Digit_Display hex_digit_display_3 (.value(outA[3:0]));  // open: dp
  Hex_Digit_Display hex_digit_display_4 (.value(outA[7:4]));  // open: dp
  _1_bit_register_main main_4 (
    .Cin(main_3_cout), .Input(outA[4]), .Enable(Enable), .Select1(FunSel[1]), .Select2(FunSel[0]),
    .Cout(main_4_cout), .Output(outA_2[4]));
  _1_bit_register_main main_5 (
    .Cin(main_4_cout), .Input(outA[5]), .Enable(Enable), .Select1(FunSel[1]), .Select2(FunSel[0]),
    .Cout(main_5_cout), .Output(outA_2[5]));
  _1_bit_register_main main_6 (
    .Cin(main_5_cout), .Input(outA[6]), .Enable(Enable), .Select1(FunSel[1]), .Select2(FunSel[0]),
    .Cout(main_6_cout), .Output(outA_2[6]));
  _1_bit_register_main main_7 (
    .Cin(main_6_cout), .Input(outA[7]), .Enable(Enable), .Select1(FunSel[1]), .Select2(FunSel[0]),
    .Output(outA_2[7]));  // open: Cout
endmodule
