// Logisim project 8-bit register.circ as structural Verilog: 1 circuit, main circuit main
module main (
  input  Select1,
  input  Select0,
  input  Enable,
  input  LSB,
  input  in_5,
  input  in_6,
  input  in_7,
  input  in_8,
  input  in_9,
  input  in_10,
  input  in_11,
  output LSB_2,
  output out_13,
  output out_14,
  output out_15,
  output out_16,
  output out_17,
  output out_18,
  output out_19,
  output out_20,
  output out_21,
  output out_22
);

  wire _1bit_Register_cout, main_1_cout, main_2_cout, main_3_cout, main_4_cout, main_5_cout, main_6_cout,
       not_1_out;

  _1_bit_register_main _1bit_Register (
    .Cin(not_1_out), .Input(LSB), .Enable(Enable), .Select1(Select1), .Select2(Select0),
    .Cout(_1bit_Register_cout), .Output(LSB_2));
  not not_1 (not_1_out, Select1);
  _1_bit_register_main main_1 (
    .Cin(_1bit_Register_cout), .Input(in_5), .Enable(Enable), .Select1(Select1), .Select2(Select0),
    .Cout(main_1_cout), .Output(out_13));
  _1_bit_register_main main_2 (
    .Cin(main_1_cout), .Input(in_6), .Enable(Enable), .Select1(Select1), .Select2(Select0),
    .Cout(main_2_cout), .Output(out_14));
  _1_bit_register_main main_3 (
    .Cin(main_2_cout), .Input(in_7), .Enable(Enable), .Select1(Select1), .Select2(Select0),
    .Cout(main_3_cout), .Output(out_15));
  _1_bit_register_main main_4 (
    .Cin(main_3_cout), .Input(in_8), .Enable(Enable), .Select1(Select1), .Select2(Select0),
    .Cout(main_4_cout), .Output(out_16));
  _1_bit_register_main main_5 (
    .Cin(main_4_cout), .Input(in_9), .Enable(Enable), .Select1(Select1), .Select2(Select0),
    .Cout(main_5_cout), .Output(out_17));
  _1_bit_register_main main_6 (
    .Cin(main_5_cout), .Input(in_10), .Enable(Enable), .Select1(Select1), .Select2(Select0),
    .Cout(main_6_cout), .Output(out_18));
  _1_bit_register_main main_7 (
    .Cin(main_6_cout), .Input(in_11), .Enable(Enable), .Select1(Select1), .Select2(Select0), .Output(out_19));  // open: Cout

  assign out_20 = Select1;
  assign out_21 = Select0;
  assign out_22 = Enable;
endmodule
