// Logisim project HWmain.circ as structural Verilog: 1 circuit, main circuit main
module main (
  input  Turn_On,
  input  in_2,
  input  in_3,
  output [3:0] ZCNO_Register,
  output [1:0] out_5,
  output [3:0] out_6,
  output [7:0] Adress,
  output [3:0] out_8,
  output [7:0] out_9,
  output [3:0] ALU,
  output [1:0] out_11,
  output [1:0] out_12,
  output [1:0] out_13,
  output [1:0] out_14,
  output [1:0] FunSel,
  output [2:0] out_16,
  output [1:0] out_17,
  output [1:0] FunSel_2
);

  wire and_1_out, and_2_out, and_4_out, and_5_out, and_18_out, and_19_out, and_20_out, and_21_out,
       and_22_out, and_23_out, and_24_out, and_25_out, and_26_out, and_70_out, and_71_out, and_72_out,
       and_73_out, and_74_out, and_75_out, and_76_out, and_77_out, and_87_out, and_88_out, and_89_out,
       and_90_out, and_91_out, and_92_out, and_93_out, and_94_out, clock_1_out, clock_2_out, clock_3_out,
       D0_I8_prime_T2, D0_I8_prime_T2_t, D0_I8_T2, D0_I8_T3, D1_T2, D1_T2_t, D1_T3, D2_I5_I8_prime_T2,
       D2_I5_I8_T2, D2_I5_prime_I8_prime_T2, D2_I5_prime_I8_T2, D2_T2, D3_T2, D3_T2_t, D4_T2, D4_T2_t, D4_T3,
       D5, D6, D7_I5_I8_prime_T3, D7_I5_I8_prime_T3_t, D7_I5_I8_T3, D7_I5_I8_T3_t, D7_I5_I8_xor_I9_I10_T3,
       D7_I5_prime_I8_prime_T3, D7_I5_prime_I8_prime_T3_t, D7_I5_prime_I8_T3, D7_I5_prime_I8_T3_t,
       D7_I8_prime_T2, D7_I8_prime_T2_t, D7_I8_prime_T4, D7_I8_prime_T4_t, D7_I8_T2, D7_I8_T2_t, D7_I8_T4,
       D7_I8_T4_t, D7_T3, D7_T4, D7_T4_t, D8_I5_I8_prime_T3, D8_I5_I8_prime_T3_t, D8_I5_I8_T3, D8_I5_I8_T3_t,
       D8_I5_I8_xor_I9_I10_T3, D8_I5_prime_I8_prime_T3, D8_I5_prime_I8_prime_T3_t, D8_I5_prime_I8_T3,
       D8_I5_prime_I8_T3_t, D8_I8_prime_T2, D8_I8_prime_T2_t, D8_I8_prime_T4, D8_I8_prime_T4_t, D8_I8_T2,
       D8_I8_T2_t, D8_I8_T4, D8_I8_T4_t, D8_T3, D8_T4, D8_T4_t, D9, D10, D11, D11_I5_I8_prime_T2,
       D11_I5_I8_prime_T2_t, D11_I5_I8_T2, D11_I5_I8_T2_t, D11_I5_I8_T3, D11_I5_I8_T3_t,
       D11_I5_prime_I8_prime_T2, D11_I5_prime_I8_prime_T2_t, D11_I5_prime_I8_T2, D11_I5_prime_I8_T2_t,
       D11_I5_prime_I8_T3, D11_I5_prime_I8_T3_t, D11_T3, D12, D12_I5_I8_prime_T2, D12_I5_I8_prime_T2_t,
       D12_I5_I8_T2, D12_I5_I8_T2_t, D12_I5_I8_T3, D12_I5_I8_T3_t, D12_I5_prime_I8_prime_T2,
       D12_I5_prime_I8_prime_T2_t, D12_I5_prime_I8_T2, D12_I5_prime_I8_T2_t, D12_I5_prime_I8_T3,
       D12_I5_prime_I8_T3_t, D12_T3, D13_I5_I8_prime_T2, D13_I5_I8_prime_T2_t, D13_I5_I8_T2, D13_I5_I8_T2_t,
       D13_I5_I8_T3, D13_I5_I8_T3_t, D13_I5_prime_I8_prime_T2, D13_I5_prime_I8_prime_T2_t,
       D13_I5_prime_I8_T2, D13_I5_prime_I8_T2_t, D13_I5_prime_I8_T3, D13_I5_prime_I8_T3_t, D13_T3, D14_T2,
       D14_T2_t, D15_Z_T2, D15_Z_T2_t, D16_Z_prime_T2, D16_Z_prime_T2_t, D17_T2, D17_T2_t, D17_T3, D17_T3_t,
       D17_T4, D17_T4_t, D18_T2, D18_T2_t, D18_T3, D18_T3_t, d_ff_5_q, decoder_7_out2, decoder_7_out3,
       decoder_7_out4, decoder_9_out0, decoder_9_out1, decoder_9_out2, decoder_9_out3, decoder_9_out4,
       decoder_9_out7, decoder_9_out8, decoder_9_out13, decoder_9_out14, decoder_9_out15, decoder_9_out16,
       decoder_9_out17, decoder_9_out18, freset, I5_I8_I11_prime_T2, I5_I8_I11_prime_T2_t,
       I5_I8_I11_prime_T3, I5_I8_I11_prime_T3_t, I5_I8_I11_T2, I5_I8_I11_T2_t, I5_I8_I11_T3, I5_I8_I11_T3_t,
       I5_I8_I11_T3_t_t, I5_I8_I11_T4, I5_I8_I11_T4_t, I5_I8_prime_I11_prime_T2, I5_I8_prime_I11_prime_T2_t,
       I5_I8_prime_I11_T2, I5_I8_prime_I11_T2_t, I5_I8_prime_I11_T3, I5_I8_prime_I11_T3_t, I5_I8_xor_I9_I10,
       I5_prime_I8_I11_prime_T2, I5_prime_I8_I11_prime_T2_t, I5_prime_I8_I11_prime_T3,
       I5_prime_I8_I11_prime_T3_t, I5_prime_I8_I11_T2, I5_prime_I8_I11_T2_t, I5_prime_I8_I11_T3,
       I5_prime_I8_I11_T3_t, I5_prime_I8_I11_T4, I5_prime_I8_I11_T4_t, I5_prime_I8_prime_I11_prime_T2,
       I5_prime_I8_prime_I11_prime_T2_t, I5_prime_I8_prime_I11_T2, I5_prime_I8_prime_I11_T3, memLoad,
       MemSelect, not_2_out, not_3_out, not_4_out, not_5_out, not_6_out, not_7_out, not_8_out, not_9_out,
       not_10_out, not_11_out, not_12_out, not_13_out, not_14_out, not_15_out, not_16_out, not_17_out,
       not_18_out, not_20_out, not_21_out, not_22_out, not_23_out, not_24_out, not_25_out, not_26_out,
       not_27_out, not_28_out, on, or_3_out, or_4_out, or_5_out, or_6_out, or_7_out, or_9_out, or_10_out,
       or_11_out, or_12_out, or_13_out, or_14_out, or_15_out, or_16_out, or_17_out, or_18_out, or_19_out,
       or_20_out, or_21_out, or_22_out, or_23_out, or_24_out, or_25_out, or_26_out, or_27_out, or_28_out,
       or_29_out, or_30_out, or_31_out, or_32_out, or_33_out, or_34_out, or_35_out, or_36_out, or_37_out,
       or_38_out, or_40_out, or_41_out, or_45_out, or_46_out, or_47_out, or_49_out, or_51_out, or_53_out,
       or_54_out, or_55_out, or_56_out, T0, T0_t, T1;
  wire [0:0] I6_I7;
  wire [1:0] adder_1_out, adder_2_out, adder_3_out, adder_4_out, adder_5_out, dFunSel, I5_I6, I6_I7_t,
       I9_I10, I9_I10_t, I12_I13, I12_I13_t, muxA_t, outBSel_t;
  wire [2:0] counter_1_q, xor_1_out;
  wire [3:0] aluFun_t, bit_extender_1_out, decoder_1_out0, decoder_2_out0, decoder_3_out0, decoder_4_out0,
       decoder_5_out0, decoder_6_out0, destDecoder, destDecoder_1, destDecoder_1_t, dRegSel, main_4_out_5_2,
       RxDecoder, RxDecoder_t, src1dec, SRC1Decoder_1, src2Decoder_1, src2Decoder_1_t, srcReg2;
  wire [3:3] multiplexer_4_out, or_39_out, or_42_out, or_43_out, or_44_out, or_48_out, or_50_out;
  wire [4:4] main_4_out_5_3;
  wire [7:0] main_1_outa, main_1_outb, main_4_out_5, multiplexer_2_out, multiplexer_3_out, ram_1_data;

  _4_registers_main main_1 (
    .FunSel(out_5), .RegSel(out_8), .Input(multiplexer_2_out), .OutASel(out_11), .OutBSel(out_12),
    .outA(main_1_outa), .outB(main_1_outb));
  or or_1 (memLoad, D17_T3, D3_T2_t, D1_T2);
  // OR_Gate or_2 has open pins: in0=D0_I8_T2, in1=D1_T2_t, in2=D4_T2_t, in3=D18_T3_t, out=open
  or or_3 (or_3_out, D0_I8_prime_T2_t, D0_I8_T2, D4_T3);
  assign out_8 = I5_prime_I8_I11_T3_t ? destDecoder_1 : 4'bz;  // Controlled_Buffer controlled_buffer_1
  assign out_8 = or_4_out ? SRC1Decoder_1 : 4'bz;  // Controlled_Buffer controlled_buffer_2
  or or_4 (or_4_out, I5_I8_prime_I11_T2_t, I5_I8_prime_I11_T2_t);
  or or_5 (or_5_out, D7_I8_prime_T2_t, D7_I8_prime_T4_t, D8_I8_prime_T2_t, D8_I8_prime_T4_t);
  assign out_8 = or_6_out ? 4'b1000 : 4'bz;  // Controlled_Buffer controlled_buffer_3
  or or_6 (or_6_out, D17_T2_t, I5_I8_I11_T2_t);
  assign out_8 = or_7_out ? src2Decoder_1_t : 4'bz;  // Controlled_Buffer controlled_buffer_4
  or or_7 (or_7_out, I5_prime_I8_I11_prime_T2, I5_I8_I11_prime_T2_t);
  assign muxA_t = D0_I8_prime_T2_t ? 2'b11 : 2'bz;  // Controlled_Buffer controlled_buffer_5
  D_Flip_Flop d_ff_1 (.clk(clock_1_out), .D(ALU[3]), .Q(ZCNO_Register[3]));  // open: Qn, preset, en, reset
  not not_1 (MemSelect, memLoad);
  or or_8 (freset, D7_I5_I8_xor_I9_I10_T3, D8_I5_I8_xor_I9_I10_T3, D0_I8_prime_T2_t, D0_I8_T2, D1_T2, I5_prime_I8_I11_T4_t, D2_T2, I5_I8_prime_I11_T3_t, D3_T2_t, D4_T3, I5_I8_prime_I11_T3_t, D11_I5_prime_I8_T3_t, I5_I8_I11_T4_t, D11_I5_I8_prime_T2_t, D11_I5_prime_I8_prime_T2_t, I5_prime_I8_I11_prime_T3_t, D11_I5_I8_T3_t, I5_I8_prime_I11_prime_T2_t, D12_I5_prime_I8_T3_t, D12_I5_I8_prime_T2_t, I5_prime_I8_prime_I11_prime_T2_t, D12_I5_I8_T3_t, I5_I8_I11_prime_T3_t, D13_I5_prime_I8_T3_t, D13_I5_I8_prime_T2_t, D13_I5_prime_I8_prime_T2_t, D13_I5_I8_T3_t, D14_T2_t, D15_Z_T2_t, D16_Z_prime_T2_t, D17_T4_t, or_9_out);
  or or_9 (or_9_out, D18_T3_t, D7_T4_t, D8_T4_t);
  or or_10 (or_10_out, D13_I5_prime_I8_prime_T2_t, D13_I5_I8_T2_t, D17_T2_t);
  assign out_5 = or_11_out ? 2'b10 : 2'bz;  // Controlled_Buffer controlled_buffer_6
  or or_11 (or_11_out, D7_I8_prime_T2_t, D8_I8_prime_T4_t);
  assign out_8 = or_3_out ? RxDecoder_t : 4'bz;  // Controlled_Buffer controlled_buffer_7
  assign out_8 = or_12_out ? destDecoder : 4'bz;  // Controlled_Buffer controlled_buffer_8
  or or_12 (or_12_out, I5_prime_I8_I11_T2_t, D2_I5_prime_I8_T2, I5_prime_I8_I11_T4_t, D2_I5_prime_I8_prime_T2, D8_I5_prime_I8_T3_t, I5_I8_prime_I11_T3_t, D7_I5_prime_I8_prime_T3_t, D11_I5_prime_I8_T2_t, D11_I5_prime_I8_T3_t, D8_I5_prime_I8_T3_t, D11_I5_prime_I8_prime_T2_t, D8_I5_prime_I8_prime_T3_t, I5_prime_I8_I11_prime_T3_t, D12_I5_prime_I8_T2_t, D12_I5_prime_I8_T3_t, I5_prime_I8_prime_I11_prime_T2_t, D12_I5_prime_I8_prime_T2_t, D13_I5_prime_I8_T2_t, D13_I5_prime_I8_T3_t, D13_I5_prime_I8_prime_T2_t);
  assign out_8 = or_5_out ? src1dec : 4'bz;  // Controlled_Buffer controlled_buffer_9
  assign out_8 = I5_I8_I11_T3_t_t ? 4'b0100 : 4'bz;  // Controlled_Buffer controlled_buffer_10
  assign out_8 = or_13_out ? 4'b0001 : 4'bz;  // Controlled_Buffer controlled_buffer_11
  or or_13 (or_13_out, D12_I5_I8_T2_t, D11_I5_I8_T2_t, D13_I5_I8_T2_t);
  assign muxA_t = or_14_out ? 2'b10 : 2'bz;  // Controlled_Buffer controlled_buffer_12
  or or_14 (or_14_out, D0_I8_T2, D4_T3);
  assign muxA_t = or_20_out ? 2'b01 : 2'bz;  // Controlled_Buffer controlled_buffer_13
  D_Flip_Flop d_ff_2 (.clk(clock_1_out), .D(ALU[2]), .Q(ZCNO_Register[2]));  // open: Qn, preset, en, reset
  assign out_17 = D18_T3_t ? 2'b01 : 2'bz;  // Controlled_Buffer controlled_buffer_14
  buf or_15 (or_15_out, D1_T2_t);  // OR_Gate
  assign out_14 = or_23_out ? 2'b10 : 2'bz;  // Controlled_Buffer controlled_buffer_15
  assign out_5 = or_16_out ? 2'b11 : 2'bz;  // Controlled_Buffer controlled_buffer_16
  or or_16 (or_16_out, D0_I8_prime_T2, D0_I8_T2, I5_prime_I8_I11_T2, I5_prime_I8_I11_T3, D2_I5_prime_I8_T2, I5_prime_I8_I11_T4_t, D2_I5_prime_I8_prime_T2, I5_I8_prime_I11_T2_t, D7_I5_prime_I8_T3_t, I5_I8_prime_I11_T2_t, D4_T3, I5_I8_prime_I11_T3_t, D7_I5_prime_I8_prime_T3_t, I5_I8_I11_T2_t, D11_I5_prime_I8_T2_t, I5_I8_I11_T3, D11_I5_prime_I8_T3_t, D8_I5_prime_I8_T3_t, I5_prime_I8_I11_prime_T2_t, D11_I5_prime_I8_prime_T2_t, D11_I5_I8_T2_t, D8_I5_prime_I8_prime_T3_t, I5_prime_I8_I11_prime_T3_t, D12_I5_prime_I8_T2_t, D12_I5_prime_I8_T3_t, I5_prime_I8_prime_I11_prime_T2_t, D12_I5_prime_I8_prime_T2_t, I5_I8_I11_prime_T2_t, D12_I5_I8_T2_t, D13_I5_prime_I8_T2_t, D13_I5_prime_I8_T3_t, or_10_out);
  assign out_5 = not_2_out ? 2'b00 : 2'bz;  // Controlled_Buffer controlled_buffer_17
  or or_17 (or_17_out, or_16_out, or_24_out, or_11_out);
  not not_2 (not_2_out, or_17_out);
  not not_3 (not_3_out, or_18_out);
  or or_18 (or_18_out, or_3_out, or_12_out, I5_prime_I8_I11_T3_t, or_4_out, or_5_out, or_6_out, I5_I8_I11_T3_t_t, or_13_out);
  assign muxA_t = not_4_out ? 2'b00 : 2'bz;  // Controlled_Buffer controlled_buffer_18
  or or_19 (or_19_out, D0_I8_prime_T2_t, or_14_out, or_20_out);
  not not_4 (not_4_out, or_19_out);
  or or_20 (or_20_out, I5_prime_I8_I11_T2_t, I5_prime_I8_I11_T3_t, D2_I5_prime_I8_T2, I5_I8_prime_I11_T2_t, D7_I5_prime_I8_T3_t, I5_I8_prime_I11_T2_t, D11_I5_prime_I8_T2_t, I5_I8_I11_T2_t, I5_I8_I11_T3_t_t, D8_I5_prime_I8_T3_t, I5_prime_I8_I11_prime_T2_t, D11_I5_I8_T2_t, D12_I5_prime_I8_T2_t, I5_I8_I11_prime_T2_t, D12_I5_I8_T2_t, D13_I5_prime_I8_T2_t, D13_I5_I8_T2_t, D17_T2_t);
  D_Flip_Flop d_ff_3 (.clk(clock_1_out), .D(ALU[1]), .Q(ZCNO_Register[1]));  // open: Qn, preset, en, reset
  alu_main main_2 (
    .FunSel(out_6), .Cin(ZCNO_Register[2]), .A(main_1_outa), .B(main_1_outb), .Output(out_9), .ZCNO(ALU));
  _3_registers_main main_3 (
    .FunSel(FunSel_2), .RegSel(out_16), .Input(multiplexer_3_out), .OutASel(out_14), .outA(Adress));
  Multiplexer #(.width(2), .disabled(0), .enable("false")) multiplexer_1 (
    .in0(dFunSel), .in1(2'b00), .out(FunSel_2), .sel(on));
  assign dFunSel = or_21_out ? 2'b01 : 2'bz;  // Controlled_Buffer controlled_buffer_19
  or or_21 (or_21_out, T1, T0, D17_T3_t, D8_I8_T4_t, D7_I8_T2_t);
  assign dFunSel = or_22_out ? 2'b10 : 2'bz;  // Controlled_Buffer controlled_buffer_20
  or or_22 (or_22_out, D3_T2_t, D18_T2_t);
  or or_23 (or_23_out, D0_I8_T2, D1_T2);
  and and_1 (and_1_out, D9, or_38_out);
  assign out_5 = or_24_out ? 2'b01 : 2'bz;  // Controlled_Buffer controlled_buffer_21
  or or_24 (or_24_out, D7_I8_prime_T4_t, D8_I8_prime_T2_t);
  assign out_8 = not_3_out ? 4'b0000 : 4'bz;  // Controlled_Buffer controlled_buffer_22
  D_Flip_Flop d_ff_4 (.clk(clock_1_out), .D(ALU[0]), .Q(ZCNO_Register[0]));  // open: Qn, preset, en, reset
  Clock clock_1 (.out(clock_1_out));
  assign dFunSel = not_5_out ? 2'b11 : 2'bz;  // Controlled_Buffer controlled_buffer_23
  not not_5 (not_5_out, or_25_out);
  or or_25 (or_25_out, or_21_out, or_30_out, or_22_out);
  assign out_17 = or_26_out ? 2'b10 : 2'bz;  // Controlled_Buffer controlled_buffer_24
  or or_26 (or_26_out, D17_T4_t, D15_Z_T2, D16_Z_prime_T2, D14_T2);
  or or_27 (or_27_out, or_26_out, D18_T3_t, or_28_out);
  assign out_17 = or_28_out ? 2'b11 : 2'bz;  // Controlled_Buffer controlled_buffer_25
  or or_28 (or_28_out, D2_I5_I8_T2, D7_I5_I8_T3_t, D8_I5_I8_T3_t);
  assign out_14 = or_29_out ? 2'b00 : 2'bz;  // Controlled_Buffer controlled_buffer_26
  or or_29 (or_29_out, T0, T1, in_2, D17_T2_t);
  assign out_14 = or_32_out ? 2'b11 : 2'bz;  // Controlled_Buffer controlled_buffer_27
  assign aluFun_t = and_1_out ? 4'b0100 : 4'bz;  // Controlled_Buffer controlled_buffer_28
  assign aluFun_t = or_33_out ? 4'b1000 : 4'bz;  // Controlled_Buffer controlled_buffer_29
  Multiplexer #(.select(2), .width(8), .enable("false")) multiplexer_2 (
    .in0(out_9), .in1(Adress), .in2(ram_1_data),
    .in3({main_4_out_5[7], I9_I10, main_4_out_5[4], I12_I13, main_4_out_5[1:0]}), .out(multiplexer_2_out),
    .sel(out_13));
  Multiplexer #(.select(2), .width(8), .enable("false")) multiplexer_3 (
    .in0(out_9), .in1(ram_1_data),
    .in2({main_4_out_5[7], I9_I10, main_4_out_5[4], I12_I13, main_4_out_5[1:0]}), .in3(Adress),
    .out(multiplexer_3_out), .sel(out_17));
  Multiplexer #(.width(4), .disabled(0), .enable("false")) multiplexer_4 (
    .in0(dRegSel), .in1(4'b1111), .out({multiplexer_4_out[3], out_16}), .sel(on));
  assign dFunSel = or_30_out ? 2'b01 : 2'bz;  // Controlled_Buffer controlled_buffer_30
  or or_30 (or_30_out, D7_I8_T4_t, D4_T2_t, D8_I8_T2_t);
  assign out_17 = not_6_out ? 2'b00 : 2'bz;  // Controlled_Buffer controlled_buffer_31
  not not_6 (not_6_out, or_27_out);
  assign out_14 = not_7_out ? I9_I10_t : 2'bz;  // Controlled_Buffer controlled_buffer_32
  or or_31 (or_31_out, or_29_out, or_23_out, or_32_out, or_40_out);
  or or_32 (or_32_out, D3_T2_t, D4_T3, D17_T3_t, D18_T3_t);
  assign aluFun_t = and_2_out ? 4'b0011 : 4'bz;  // Controlled_Buffer controlled_buffer_33
  and and_2 (and_2_out, D6, or_38_out);
  or or_33 (or_33_out, D12_I5_prime_I8_T3_t, D12_I5_I8_prime_T2_t, D12_I5_prime_I8_prime_T2_t, D12_I5_I8_T3_t, D13_I5_prime_I8_T3_t, D13_I5_I8_prime_T2_t, D13_I5_prime_I8_prime_T2_t, D13_I5_I8_T3_t);
  assign dRegSel = or_34_out ? 4'b0100 : 4'bz;  // Controlled_Buffer controlled_buffer_34
  or or_34 (or_34_out, T0_t, T1, D14_T2, D18_T3_t, D15_Z_T2_t, D17_T4, D16_Z_prime_T2_t);
  assign dRegSel = in_3 ? 4'b0010 : 4'bz;  // Controlled_Buffer controlled_buffer_35
  assign dRegSel = or_35_out ? destDecoder : 4'bz;  // Controlled_Buffer controlled_buffer_36
  or or_35 (or_35_out, D2_I5_I8_prime_T2, I5_I8_prime_I11_T3_t, D7_I5_I8_prime_T3_t, I5_I8_I11_T4_t, D11_I5_I8_prime_T2_t, D8_I5_I8_prime_T3_t, D11_I5_I8_T3_t, I5_I8_prime_I11_prime_T2_t, D12_I5_I8_prime_T2_t, I5_I8_I11_prime_T3_t, D12_I5_I8_T3_t, D13_I5_I8_prime_T2_t, D13_I5_I8_T3_t);
  assign dRegSel = or_36_out ? 4'b0001 : 4'bz;  // Controlled_Buffer controlled_buffer_37
  or or_36 (or_36_out, D3_T2_t, D4_T2_t, D17_T3_t, D18_T2_t);
  assign dRegSel = or_37_out ? src1dec : 4'bz;  // Controlled_Buffer controlled_buffer_38
  or or_37 (or_37_out, D7_I8_T2_t, D7_I8_prime_T4_t, D8_I8_T2_t, D8_I8_prime_T4_t);
  assign xor_1_out = {main_4_out_5[4], I12_I13} ^ {main_4_out_5[7], I9_I10};  // XOR_Gate xor_1, 3 bits wide
  not not_7 (not_7_out, or_31_out);
  not not_8 (not_8_out, xor_1_out[1]);
  not not_9 (not_9_out, xor_1_out[2]);
  not not_10 (not_10_out, xor_1_out[0]);
  and and_3 (I5_I8_xor_I9_I10, not_9_out, not_8_out, not_10_out);
  assign out_14 = or_40_out ? I12_I13 : 2'bz;  // Controlled_Buffer controlled_buffer_39
  assign aluFun_t = and_4_out ? 4'b0001 : 4'bz;  // Controlled_Buffer controlled_buffer_40
  and and_4 (and_4_out, D5, or_38_out);
  or or_38 (or_38_out, I5_prime_I8_I11_T4_t, I5_I8_prime_I11_T3_t, I5_I8_I11_T4_t, I5_prime_I8_I11_prime_T3_t, I5_I8_prime_I11_prime_T2, I5_prime_I8_prime_I11_prime_T2, I5_I8_I11_prime_T3);
  Hex_Digit_Display hex_digit_display_1 (.value(bit_extender_1_out));  // open: dp
  assign bit_extender_1_out = {{3{1'b0}}, main_4_out_5_3[4]};  // Bit_Extender bit_extender_1
  Clock clock_2 (.out(clock_2_out));
  Decoder #(.select(2), .enable("false")) decoder_1 (
    .out0(decoder_1_out0[0]), .out1(decoder_1_out0[1]), .out2(decoder_1_out0[2]), .out3(decoder_1_out0[3]),
    .sel({I5_I6[0], I6_I7[0]}));
  or or_39 (or_39_out[3], decoder_1_out0[0], decoder_1_out0[1]);
  or or_40 (or_40_out, I5_prime_I8_I11_T3_t, I5_I8_prime_I11_T2_t, I5_I8_prime_I11_T2_t, I5_I8_I11_T3_t_t);
  assign aluFun_t = and_5_out ? 4'b0101 : 4'bz;  // Controlled_Buffer controlled_buffer_41
  and and_5 (and_5_out, D10, or_38_out);
  assign aluFun_t = or_46_out ? 4'b0110 : 4'bz;  // Controlled_Buffer controlled_buffer_42
  and and_6 (D7_I5_I8_xor_I9_I10_T3, I5_I8_xor_I9_I10, decoder_7_out3, decoder_9_out7);
  and and_7 (D8_I5_I8_xor_I9_I10_T3, I5_I8_xor_I9_I10, decoder_7_out3, decoder_7_out4);
  or or_41 (or_41_out, or_34_out, in_3, or_35_out, or_36_out, or_37_out);
  not not_11 (not_11_out, or_41_out);
  assign dRegSel = not_11_out ? 4'b0000 : 4'bz;  // Controlled_Buffer controlled_buffer_43
  Hex_Digit_Display hex_digit_display_2 (.value(main_4_out_5_2));  // open: dp
  RAM #(.bus("separate")) ram_1 (
    .addr(Adress), .din(out_9), .data(ram_1_data), .str(memLoad), .sel(Turn_On), .clk(clock_2_out),
    .ld(MemSelect));  // open: clr
  assign destDecoder = not_12_out ? decoder_1_out0 : 4'bz;  // Controlled_Buffer controlled_buffer_44
  not not_12 (not_12_out, I5_I6[1]);
  assign destDecoder = I5_I6[1] ? {{2{or_39_out[3]}}, decoder_1_out0[2], decoder_1_out0[3]} : 4'bz;  // Controlled_Buffer controlled_buffer_45
  Decoder #(.select(2), .enable("false")) decoder_2 (
    .out0(decoder_2_out0[0]), .out1(decoder_2_out0[1]), .out2(decoder_2_out0[2]), .out3(decoder_2_out0[3]),
    .sel(adder_1_out));
  Adder #(.width(2)) adder_1 (.a({I5_I6[0], I6_I7[0]}), .b(2'b01), .out(adder_1_out));  // open: cin, cout
  not not_13 (not_13_out, I5_I6[1]);
  or or_42 (or_42_out[3], decoder_2_out0[0], decoder_2_out0[1]);
  Adder #(.width(2)) adder_2 (.a(I9_I10), .b(2'b01), .out(adder_2_out));  // open: cin, cout
  Decoder #(.select(2), .enable("false")) decoder_3 (
    .out0(decoder_3_out0[0]), .out1(decoder_3_out0[1]), .out2(decoder_3_out0[2]), .out3(decoder_3_out0[3]),
    .sel(adder_2_out));
  not not_14 (not_14_out, main_4_out_5[7]);
  or or_43 (or_43_out[3], decoder_3_out0[0], decoder_3_out0[1]);
  Decoder #(.select(2), .enable("false")) decoder_4 (
    .out0(decoder_4_out0[0]), .out1(decoder_4_out0[1]), .out2(decoder_4_out0[2]), .out3(decoder_4_out0[3]),
    .sel(adder_3_out));
  Adder #(.width(2)) adder_3 (.a(I12_I13), .b(2'b01), .out(adder_3_out));  // open: cin, cout
  not not_15 (not_15_out, main_4_out_5[4]);
  or or_44 (or_44_out[3], decoder_4_out0[0], decoder_4_out0[1]);
  assign aluFun_t = not_16_out ? 4'b0000 : 4'bz;  // Controlled_Buffer controlled_buffer_46
  not not_16 (not_16_out, or_45_out);
  or or_45 (or_45_out, and_4_out, and_2_out, and_1_out, and_5_out, or_33_out, or_46_out);
  or or_46 (or_46_out, D11_I5_prime_I8_T3_t, D11_I5_I8_prime_T2_t, D11_I5_prime_I8_prime_T2_t, D11_I5_I8_T3_t);
  and and_8 (D7_I8_T2, main_4_out_5[7], decoder_7_out2, decoder_9_out7);
  and and_9 (D7_I8_prime_T2, not_20_out, decoder_7_out2, decoder_9_out7);
  and and_10 (D7_I8_T4, main_4_out_5[7], decoder_7_out4, decoder_9_out7);
  and and_11 (D7_I8_prime_T4, not_20_out, decoder_7_out4, decoder_9_out7);
  and and_12 (D8_I8_T2, main_4_out_5[7], decoder_7_out2, decoder_9_out8);
  and and_13 (D8_I8_prime_T2, not_20_out, decoder_7_out2, decoder_9_out8);
  and and_14 (D8_I8_T4, main_4_out_5[7], decoder_9_out8, decoder_7_out4);
  and and_15 (D8_I8_prime_T4, not_20_out, decoder_9_out8, decoder_7_out4);
  and and_16 (D7_T4, decoder_7_out4, decoder_9_out7);
  and and_17 (D8_T4, decoder_7_out4, decoder_9_out8);
  assign out_11 = or_47_out ? I5_I6 : 2'bz;  // Controlled_Buffer controlled_buffer_47
  or or_47 (or_47_out, D1_T2, D3_T2_t);
  assign out_11 = or_51_out ? I6_I7_t : 2'bz;  // Controlled_Buffer controlled_buffer_48
  _16_bit_IR_register_main main_4 (
    .out_5({main_4_out_5_3[4], main_4_out_5_2, I5_I6, I6_I7[0], main_4_out_5[7], I9_I10, main_4_out_5[4], I12_I13, main_4_out_5[1:0]}),
    .Enable(FunSel[1]), .Funcel({2{FunSel[1]}}), .L1_H0(T1), .in_4(ram_1_data));
  Decoder #(.select(2), .enable("false")) decoder_5 (
    .out0(decoder_5_out0[0]), .out1(decoder_5_out0[1]), .out2(decoder_5_out0[2]), .out3(decoder_5_out0[3]),
    .sel(I9_I10));
  assign src1dec = not_17_out ? decoder_5_out0 : 4'bz;  // Controlled_Buffer controlled_buffer_49
  not not_17 (not_17_out, main_4_out_5[7]);
  or or_48 (or_48_out[3], decoder_5_out0[0], decoder_5_out0[1]);
  assign src1dec = main_4_out_5[7] ? {{2{or_48_out[3]}}, decoder_5_out0[2], decoder_5_out0[3]} : 4'bz;  // Controlled_Buffer controlled_buffer_50
  not not_18 (not_18_out, I5_I6[1]);
  assign destDecoder_1_t = not_13_out ? decoder_2_out0 : 4'bz;  // Controlled_Buffer controlled_buffer_51
  assign destDecoder_1_t = I5_I6[1] ? {{2{or_42_out[3]}}, decoder_2_out0[2], decoder_2_out0[3]} : 4'bz;  // Controlled_Buffer controlled_buffer_52
  assign SRC1Decoder_1 = not_14_out ? decoder_3_out0 : 4'bz;  // Controlled_Buffer controlled_buffer_53
  assign SRC1Decoder_1 = main_4_out_5[7] ? {{2{or_43_out[3]}}, decoder_3_out0[2], decoder_3_out0[3]} : 4'bz;  // Controlled_Buffer controlled_buffer_54
  assign src2Decoder_1 = not_15_out ? decoder_4_out0 : 4'bz;  // Controlled_Buffer controlled_buffer_55
  assign src2Decoder_1 = main_4_out_5[4] ? {{2{or_44_out[3]}}, decoder_4_out0[2], decoder_4_out0[3]} : 4'bz;  // Controlled_Buffer controlled_buffer_56
  assign out_11 = I5_I8_I11_T4_t ? 2'b00 : 2'bz;  // Controlled_Buffer controlled_buffer_57
  not not_19 (on, Turn_On);
  or or_49 (or_49_out, on, freset);
  Decoder #(.select(2), .enable("false")) decoder_6 (
    .out0(decoder_6_out0[0]), .out1(decoder_6_out0[1]), .out2(decoder_6_out0[2]), .out3(decoder_6_out0[3]),
    .sel(I12_I13));
  or or_50 (or_50_out[3], decoder_6_out0[0], decoder_6_out0[1]);
  not not_20 (not_20_out, main_4_out_5[7]);
  and and_18 (and_18_out, not_18_out, decoder_7_out3, main_4_out_5[7]);
  and and_19 (and_19_out, I5_I6[1], decoder_7_out3, not_20_out);
  and and_20 (and_20_out, not_20_out, decoder_7_out3, not_18_out);
  and and_21 (and_21_out, main_4_out_5[7], decoder_7_out3, I5_I6[1]);
  assign out_11 = I5_I8_I11_T4_t ? I12_I13_t : 2'bz;  // Controlled_Buffer controlled_buffer_58
  or or_51 (or_51_out, I5_prime_I8_I11_T4_t, D11_I5_prime_I8_T3_t, D12_I5_prime_I8_T3_t, D13_I5_prime_I8_T3_t);
  D_Flip_Flop d_ff_5 (.clk(clock_3_out), .D(or_49_out), .Q(d_ff_5_q));  // open: Qn, preset, en, reset
  assign srcReg2 = not_21_out ? decoder_6_out0 : 4'bz;  // Controlled_Buffer controlled_buffer_59
  not not_21 (not_21_out, main_4_out_5[4]);
  assign srcReg2 = main_4_out_5[4] ? {{2{or_50_out[3]}}, decoder_6_out0[2], decoder_6_out0[3]} : 4'bz;  // Controlled_Buffer controlled_buffer_60
  and and_22 (and_22_out, not_18_out, decoder_7_out2, main_4_out_5[7]);
  and and_23 (and_23_out, I5_I6[1], decoder_7_out2, not_20_out);
  and and_24 (and_24_out, not_20_out, decoder_7_out2, not_18_out);
  and and_25 (and_25_out, main_4_out_5[7], decoder_7_out2, I5_I6[1]);
  assign out_11 = or_54_out ? 2'b11 : 2'bz;  // Controlled_Buffer controlled_buffer_61
  Decoder #(.select(3), .enable("false")) decoder_7 (
    .out0(T0), .out1(T1), .out2(decoder_7_out2), .out3(decoder_7_out3), .out4(decoder_7_out4),
    .sel(counter_1_q));  // open: out5, out6, out7
  Counter #(.width(3), .max('h4), .trigger("falling")) counter_1 (
    .count(Turn_On), .Q(counter_1_q), .clk(clock_3_out), .clr(d_ff_5_q));  // open: load, D, carry
  Clock clock_3 (.out(clock_3_out));
  or or_52 (FunSel[1], T0, T1);
  Decoder #(.select(2), .enable("false")) decoder_8 (
    .out0(RxDecoder[0]), .out1(RxDecoder[1]), .out2(RxDecoder[2]), .out3(RxDecoder[3]), .sel(I5_I6));
  not not_22 (not_22_out, I6_I7[0]);
  and and_26 (and_26_out, decoder_9_out0, decoder_7_out2);
  and and_27 (D2_T2, decoder_9_out2, decoder_7_out2);
  and and_28 (D2_I5_prime_I8_T2, decoder_9_out2, and_22_out);
  and and_29 (D2_I5_I8_prime_T2, decoder_9_out2, and_23_out);
  and and_30 (D2_I5_prime_I8_prime_T2, decoder_9_out2, and_24_out);
  and and_31 (D2_I5_I8_T2, decoder_9_out2, and_25_out);
  and and_32 (D11_I5_prime_I8_T2, D11, and_22_out);
  and and_33 (D11_I5_prime_I8_T3, D11, and_18_out);
  and and_34 (D11_I5_I8_prime_T2, D11, and_23_out);
  and and_35 (D11_I5_prime_I8_prime_T2, D11, and_24_out);
  and and_36 (D11_I5_I8_T2, D11, and_25_out);
  and and_37 (D11_I5_I8_T3, D11, and_21_out);
  and and_38 (D12_I5_prime_I8_T2, D12, and_22_out);
  and and_39 (D12_I5_prime_I8_T3, D12, and_18_out);
  and and_40 (D12_I5_I8_prime_T2, D12, and_23_out);
  and and_41 (D12_I5_prime_I8_prime_T2, D12, and_24_out);
  and and_42 (D12_I5_I8_T2, D12, and_25_out);
  and and_43 (D12_I5_I8_T3, D12, and_21_out);
  and and_44 (D13_I5_prime_I8_T3, decoder_9_out13, and_18_out);
  and and_45 (D13_I5_prime_I8_T2, decoder_9_out13, and_22_out);
  and and_46 (D13_I5_I8_prime_T2, decoder_9_out13, and_23_out);
  and and_47 (D13_I5_prime_I8_prime_T2, decoder_9_out13, and_24_out);
  and and_48 (D13_I5_I8_T2, decoder_9_out13, and_25_out);
  and and_49 (D13_I5_I8_T3, decoder_9_out13, and_21_out);
  and and_50 (D7_I5_prime_I8_T3, decoder_9_out7, and_18_out);
  and and_51 (D7_I5_I8_prime_T3, decoder_9_out7, and_19_out);
  and and_52 (D7_I5_prime_I8_prime_T3, decoder_9_out7, and_20_out);
  and and_53 (D7_I5_I8_T3, decoder_9_out7, and_21_out);
  and and_54 (D8_I5_prime_I8_T3, decoder_9_out8, and_18_out);
  and and_55 (D8_I5_I8_prime_T3, decoder_9_out8, and_19_out);
  and and_56 (D8_I5_prime_I8_prime_T3, decoder_9_out8, and_20_out);
  and and_57 (D8_I5_I8_T3, decoder_9_out8, and_21_out);
  not not_23 (not_23_out, or_53_out);
  or or_53 (or_53_out, I5_I8_I11_T4_t, or_47_out, I5_I8_I11_T4_t, or_51_out, or_54_out);
  assign out_11 = not_23_out ? I9_I10_t : 2'bz;  // Controlled_Buffer controlled_buffer_62
  or or_54 (or_54_out, D11_I5_I8_T3_t, D12_I5_I8_T3_t, D13_I5_I8_T3_t, D17_T3_t);
  and and_58 (D0_I8_prime_T2, not_22_out, and_26_out);
  and and_59 (D0_I8_T2, I6_I7[0], and_26_out);
  and and_60 (D0_I8_T3, decoder_9_out0, I6_I7[0], decoder_7_out3);
  and and_61 (D1_T2, decoder_9_out1, decoder_7_out2);
  and and_62 (D1_T3, decoder_9_out1, decoder_7_out3);
  and and_63 (D3_T2, decoder_7_out2, decoder_9_out3);
  and and_64 (D4_T2, decoder_7_out2, decoder_9_out4);
  and and_65 (D11_T3, D11, decoder_7_out3);
  and and_66 (D12_T3, D12, decoder_7_out3);
  and and_67 (D13_T3, decoder_9_out13, decoder_7_out3);
  and and_68 (D7_T3, decoder_7_out3, decoder_9_out7);
  and and_69 (D8_T3, decoder_9_out8, decoder_7_out3);
  Decoder #(.select(5), .disabled(0), .enable("false")) decoder_9 (
    .out0(decoder_9_out0), .out1(decoder_9_out1), .out2(decoder_9_out2), .out3(decoder_9_out3),
    .out4(decoder_9_out4), .out5(D5), .out6(D6), .out7(decoder_9_out7), .out8(decoder_9_out8), .out9(D9),
    .out10(D10), .out11(D11), .out12(D12), .out13(decoder_9_out13), .out14(decoder_9_out14),
    .out15(decoder_9_out15), .out16(decoder_9_out16), .out17(decoder_9_out17), .out18(decoder_9_out18),
    .sel({main_4_out_5_3[4], main_4_out_5_2}));  // open: out19, out20, out21, out22, out23, out24, out25, out26, out27, out28, out29, out30, out31
  not not_24 (not_24_out, ZCNO_Register[3]);
  assign outBSel_t = I5_prime_I8_I11_T4_t ? adder_4_out : 2'bz;  // Controlled_Buffer controlled_buffer_63
  Adder #(.width(2)) adder_4 (.a({I5_I6[0], I6_I7[0]}), .b(2'b01), .out(adder_4_out));  // open: cin, cout
  not not_25 (not_25_out, I5_I6[1]);
  assign outBSel_t = I5_I8_I11_T4_t ? 2'b01 : 2'bz;  // Controlled_Buffer controlled_buffer_64
  Adder #(.width(2)) adder_5 (.a(I12_I13_t), .b(2'b01), .out(adder_5_out));  // open: cin, cout
  assign outBSel_t = I5_prime_I8_I11_prime_T3_t ? adder_5_out : 2'bz;  // Controlled_Buffer controlled_buffer_65
  or or_55 (or_55_out, D10, D9, D6, D5);
  and and_70 (and_70_out, not_25_out, main_4_out_5[7], main_4_out_5[4]);
  and and_71 (and_71_out, I5_I6[1], not_27_out, main_4_out_5[4]);
  and and_72 (and_72_out, not_25_out, not_27_out, main_4_out_5[4]);
  and and_73 (and_73_out, I5_I6[1], main_4_out_5[7], main_4_out_5[4]);
  and and_74 (and_74_out, not_25_out, main_4_out_5[7], not_26_out);
  and and_75 (and_75_out, I5_I6[1], not_27_out, not_26_out);
  and and_76 (and_76_out, not_25_out, not_27_out, not_26_out);
  and and_77 (and_77_out, I5_I6[1], main_4_out_5[7], not_26_out);
  not not_26 (not_26_out, main_4_out_5[4]);
  not not_27 (not_27_out, main_4_out_5[7]);
  and and_78 (D4_T3, decoder_9_out4, decoder_7_out3);
  and and_79 (D14_T2, decoder_7_out2, decoder_9_out14);
  and and_80 (D15_Z_T2, decoder_9_out15, decoder_7_out2, ZCNO_Register[3]);
  and and_81 (D16_Z_prime_T2, decoder_9_out16, not_24_out, decoder_7_out2);
  and and_82 (D17_T2, decoder_9_out17, decoder_7_out2);
  and and_83 (D17_T3, decoder_9_out17, decoder_7_out3);
  and and_84 (D17_T4, decoder_9_out17, decoder_7_out4);
  and and_85 (D18_T2, decoder_9_out18, decoder_7_out2);
  and and_86 (D18_T3, decoder_9_out18, decoder_7_out3);
  or or_56 (or_56_out, I5_I8_I11_T4_t, I5_prime_I8_I11_T4_t, I5_prime_I8_I11_prime_T3_t);
  and and_87 (and_87_out, or_55_out, and_70_out);
  and and_88 (and_88_out, or_55_out, and_71_out);
  and and_89 (and_89_out, or_55_out, and_72_out);
  and and_90 (and_90_out, or_55_out, and_73_out);
  and and_91 (and_91_out, or_55_out, and_74_out);
  and and_92 (and_92_out, or_55_out, and_75_out);
  and and_93 (and_93_out, or_55_out, and_76_out);
  and and_94 (and_94_out, or_55_out, and_77_out);
  not not_28 (not_28_out, or_56_out);
  assign outBSel_t = not_28_out ? I12_I13_t : 2'bz;  // Controlled_Buffer controlled_buffer_66
  and and_95 (I5_prime_I8_I11_T2, decoder_7_out2, and_87_out);
  and and_96 (I5_prime_I8_I11_T3, decoder_7_out3, and_87_out);
  and and_97 (I5_prime_I8_I11_T4, decoder_7_out4, and_87_out);
  and and_98 (I5_I8_prime_I11_T2, decoder_7_out2, and_88_out);
  and and_99 (I5_I8_prime_I11_T3, decoder_7_out3, and_88_out);
  and and_100 (I5_prime_I8_prime_I11_T2, decoder_7_out2, and_89_out);
  and and_101 (I5_prime_I8_prime_I11_T3, decoder_7_out3, and_89_out);
  and and_102 (I5_I8_I11_T2, decoder_7_out2, and_90_out);
  and and_103 (I5_I8_I11_T3_t, decoder_7_out3, and_90_out);
  and and_104 (I5_I8_I11_T4, decoder_7_out4, and_90_out);
  and and_105 (I5_prime_I8_I11_prime_T2, decoder_7_out2, and_91_out);
  and and_106 (I5_prime_I8_I11_prime_T3, decoder_7_out3, and_91_out);
  and and_107 (I5_I8_prime_I11_prime_T2, decoder_7_out2, and_92_out);
  and and_108 (I5_prime_I8_prime_I11_prime_T2, and_93_out, decoder_7_out2);
  and and_109 (I5_I8_I11_prime_T2, decoder_7_out2, and_94_out);
  and and_110 (I5_I8_I11_prime_T3, decoder_7_out3, and_94_out);

  assign FunSel[0] = FunSel[1];

  // Other names for the same wires on the sheet: I6_I7[1] = I5_I6[0]; aluFun[3:0] = out_6; gFunSel[1:0] = out_5;
  //   gRegSel[3:0] = out_8; muxA[1:0] = out_13; MuxB[1:0] = out_17; outASel[1:0] = out_11; outBSel[1:0] = out_12;
  //   outCSel[1:0] = out_14; z = ZCNO_Register[3]

  // Notes on the sheet:
  //   Address
  //   ZCNO
  //   MuxA
  //   Output
  //   opCode
  //   L/H
  //   Part2c-16bitIRRegister
endmodule
