// Logisim project borg hw2.circ as structural Verilog: 1 circuit, main circuit main
module main (
  input  [3:0] FunSel,
  input  Cin,
  input  [7:0] A,
  input  [7:0] B,
  output [7:0] Output,
  output [3:0] ZCNO
);

  wire adder_1_cout, adder_2_cout, adder_3_cout, not_3_out, or_2_out;
  wire [0:0] undriven;
  wire [1:0] adder_5_cout, adder_6_cout, xor_3_out, xor_4_out;
  wire [1:1] undriven_2, undriven_3;
  wire [6:0] adder_1_out, adder_2_out, adder_3_out;
  wire [7:0] and_1_out, not_1_out, not_2_out, or_1_out, xor_1_out, xor_2_out;
  wire [7:7] adder_4_out, adder_5_out, adder_6_out;

  assign xor_1_out = B ^ {8{1'b1}};  // XOR_Gate xor_1, 8 bits wide
  Adder #(.width(7)) adder_1 (.a(A[6:0]), .b(B[6:0]), .out(adder_1_out), .cin(Cin), .cout(adder_1_cout));
  Adder #(.width(7)) adder_2 (.a(A[6:0]), .b(B[6:0]), .out(adder_2_out), .cout(adder_2_cout));  // open: cin
  Adder #(.width(7)) adder_3 (.a(A[6:0]), .b(xor_1_out[6:0]), .out(adder_3_out), .cin(1'b1), .cout(adder_3_cout));
  assign and_1_out = A & B;  // AND_Gate and_1, 8 bits wide
  assign or_1_out = A | B;  // OR_Gate or_1, 8 bits wide
  assign not_1_out = ~A;  // NOT_Gate not_1, 8 bits wide
  assign xor_2_out = A ^ B;  // XOR_Gate xor_2, 8 bits wide
  assign not_2_out = ~B;  // NOT_Gate not_2, 8 bits wide
  Adder #(.width(1)) adder_4 (.a(A[7]), .b(B[7]), .out(adder_4_out[7]), .cin(adder_1_cout), .cout(xor_4_out[1]));
  Adder #(.width(1)) adder_5 (.a(A[7]), .b(B[7]), .out(adder_5_out[7]), .cin(adder_2_cout), .cout(adder_5_cout[0]));
  Adder #(.width(1)) adder_6 (
    .a(A[7]), .b(xor_1_out[7]), .out(adder_6_out[7]), .cin(adder_3_cout), .cout(adder_6_cout[0]));
  xor xor_3 (xor_3_out[0], A[6], A[7]);
  xor xor_4 (xor_4_out[0], xor_4_out[1], adder_1_cout);
  xor xor_5 (adder_5_cout[1], adder_5_cout[0], adder_2_cout);
  xor xor_6 (adder_6_cout[1], adder_6_cout[0], adder_3_cout);
  Multiplexer #(.select(4), .width(8), .disabled(0), .enable("false")) multiplexer_1 (
    .in0(A), .in1({adder_5_out[7], adder_2_out}), .in2({adder_4_out[7], adder_1_out}),
    .in3({adder_6_out[7], adder_3_out}), .in4(and_1_out), .in5(or_1_out), .in6(not_1_out), .in7(xor_2_out),
    .in8({A[6:0], 1'b0}), .in9({1'b0, A[7:1]}), .in10({A[6:0], 1'b0}), .in11({{2{A[7]}}, A[6:1]}),
    .in12({Cin, A[7:1]}), .in13({A[6:0], Cin}), .in14(B), .in15(not_2_out), .out(Output), .sel(FunSel));
  not not_3 (not_3_out, Output[7]);
  Multiplexer #(.select(4), .width(2)) multiplexer_2 (
    .in1(xor_4_out), .in2(adder_5_cout), .in3(adder_6_cout), .in8({A[7], undriven[0]}),
    .in9({undriven_2[1], A[0]}), .in10(xor_3_out), .in11({undriven_3[1], A[0]}), .in12({2{A[0]}}),
    .in13({2{A[7]}}), .out({ZCNO[2], ZCNO[0]}), .sel(FunSel));  // open: in0, in4, in5, in6, in7, in14, in15, en
  or or_2 (or_2_out, Output[7], Output[6], Output[5], Output[4], Output[3], Output[2], Output[1], Output[0]);
  not not_4 (ZCNO[3], or_2_out);
  Multiplexer #(.select(4)) multiplexer_3 (
    .in0(not_3_out), .in1(not_3_out), .in2(not_3_out), .in3(not_3_out), .in4(not_3_out), .in5(not_3_out),
    .in6(not_3_out), .in7(not_3_out), .in8(not_3_out), .in9(not_3_out), .in10(not_3_out), .in12(not_3_out),
    .in13(not_3_out), .in14(not_3_out), .in15(not_3_out), .out(ZCNO[1]), .sel(FunSel));  // open: in11, en
endmodule
